# Fritzing sketch Circuit Design (saved by Fritzing 0.9.3b)

parts:
  Part1 = Arduino Uno (Rev3)
  M1 = DC Motor
  M2 = DC Motor
  Part2 = InvenSense MPU6050
  S1 = H-Bridge with L298N
  VCC2 = Battery

nets:
  N1: Part1.A4/SDA, Part2.SDA
  N2: Part1.A5/SCL, Part2.SCL
  N3: Part1.D9_PWM, S1.IN3
  N4: Part1.D10_PWM/SS, S1.IN2
  N5: Part1.D11_PWM/MOSI, S1.IN1
  N6: Part1.D2, Part2.INT
  N7: Part1.D6_PWM, S1.IN4
  5V: Part1.5V, Part2.VCC
  GND: Part1.GND, Part2.GND, S1.GND, VCC2.-
  VIN: Part1.VIN, S1.12V, VCC2.+
  N8: M1.pin_1, S1.M1-02
  N9: M1.pin_2, S1.M1-01
  N10: M2.pin_1, S1.M2-02
  N11: M2.pin_2, S1.M2-01

custom parts:
  H-Bridge with L298N: h-bridge
  Battery: Your standard 3x 18650 battery pack (11.1 Volts)
